// Logisim project sqrt2.circ as structural Verilog: 37 circuits, main circuit main
module main (
  input  ENABLE,
  input  [15:0] IO_DATA_IN,
  output NAN,
  output PINF,
  output NINF,
  output RESULT,
  output [15:0] IO_DATA_OUT
);

  wire CLK_out;

  Clock CLK (.out(CLK_out));
  sqrt sqrt_1 (
    .CLK(CLK_out), .ENABLE(ENABLE), .IO_DATA_IN(IO_DATA_IN), .IS_NAN(NAN), .IS_PINF(PINF), .IS_NINF(NINF),
    .RESULT(RESULT), .IO_DATA_OUT(IO_DATA_OUT));
endmodule

module sqrt (
  input  CLK,
  input  ENABLE,
  input  [15:0] IO_DATA_IN,
  output IS_NAN,
  output IS_PINF,
  output IS_NINF,
  output RESULT,
  output [15:0] IO_DATA_OUT
);

  wire and_2_out, BYPASS_CORE, calc_sqrt_1_result, input_parser_1_is_inf, input_parser_1_is_nan,
       input_parser_1_is_zero, input_parser_1_sign, nor_1_out, not_1_out, SHOULD_SAVE_DATA;
  wire [4:0] EXP, exp_mant_normalizer_1_norm_exp, ODD_EXP;
  wire [7:0] COUNTER;
  wire [9:0] MANT;
  wire [10:0] MANT_SQRT;
  wire [15:0] ANSWER, assemble_answer_1_answer, exp_mant_normalizer_1_norm_mant, exp_to_odd_1_new_mant,
       memory_16bits_1_val, SPECIAL_OUT;

  // Probe on COUNTER
  clk_counter clk_counter_1 (.CLK(CLK), .ENABLE(ENABLE), .VAL(COUNTER));
  // Probe on memory_16bits_1_val
  memory_16bits memory_16bits_1 (.DATA(IO_DATA_IN), .C(SHOULD_SAVE_DATA), .ENABLE(ENABLE), .VAL(memory_16bits_1_val));
  // Probe on ANSWER
  Transistor #(.\type ("n"), .width(16)) transistor_1 (.in(ANSWER), .out(IO_DATA_IN), .gate(RESULT));
  nor nor_1 (nor_1_out, COUNTER[0], COUNTER[1], COUNTER[2], COUNTER[3], COUNTER[4], COUNTER[5], COUNTER[6], COUNTER[7]);
  input_parser input_parser_1 (
    .N(memory_16bits_1_val), .Mant(MANT), .Exp(EXP), .Sign(input_parser_1_sign),
    .IS_ZERO(input_parser_1_is_zero), .IS_NAN(input_parser_1_is_nan), .IS_INF(input_parser_1_is_inf));
  not not_1 (not_1_out, RESULT);
  Transistor #(.width(16)) transistor_2 (.in(ANSWER), .out(IO_DATA_IN), .gate(not_1_out));
  and and_1 (SHOULD_SAVE_DATA, nor_1_out, CLK);
  // Probe on MANT
  // Probe on EXP
  // Probe on SPECIAL_OUT
  special_case_handler special_case_handler_1 (
    .N(memory_16bits_1_val), .Sign(input_parser_1_sign), .IS_ZERO_INP(input_parser_1_is_zero),
    .IS_NAN_INP(input_parser_1_is_nan), .IS_INF_INP(input_parser_1_is_inf), .SPECIAL_OUT(SPECIAL_OUT),
    .IS_PINF(IS_PINF), .IS_NAN(IS_NAN), .IS_NINF(IS_NINF), .BYPASS_CORE(BYPASS_CORE));
  // Probe on exp_mant_normalizer_1_norm_mant
  exp_mant_normalizer exp_mant_normalizer_1 (
    .MANT(MANT), .EXP(EXP), .ENABLE(ENABLE), .NORM_MANT(exp_mant_normalizer_1_norm_mant),
    .NORM_EXP(exp_mant_normalizer_1_norm_exp));
  // Probe on exp_mant_normalizer_1_norm_exp
  and and_2 (and_2_out, BYPASS_CORE, SHOULD_SAVE_DATA);
  or or_1 (RESULT, and_2_out, calc_sqrt_1_result);
  exp_to_odd exp_to_odd_1 (
    .MANT(exp_mant_normalizer_1_norm_mant), .EXP(exp_mant_normalizer_1_norm_exp),
    .NEW_MANT(exp_to_odd_1_new_mant), .NEW_EXP(ODD_EXP));
  // Probe on ODD_EXP
  // Probe on MANT_SQRT
  // Probe on ODD_EXP
  // Probe on exp_to_odd_1_new_mant
  assemble_answer assemble_answer_1 (.MANT_SQRT(MANT_SQRT), .ODD_EXP(ODD_EXP), .ANSWER(assemble_answer_1_answer));
  calc_sqrt calc_sqrt_1 (
    .MANT(exp_to_odd_1_new_mant), .COUNTER(COUNTER), .CLK(CLK), .ENABLE(ENABLE), .RESULT(calc_sqrt_1_result),
    .MANT_SQRT(MANT_SQRT));
  // Probe on MANT_SQRT
  // Probe on ANSWER
  mux_2to1_16bit mux_2to1_16bit_1 (.D1(SPECIAL_OUT), .D0(assemble_answer_1_answer), .COND(BYPASS_CORE), .RES(ANSWER));

  assign IO_DATA_OUT = IO_DATA_IN;
  // also tied to GND on the sheet: {IO_DATA_IN[0], IO_DATA_IN[1], IO_DATA_IN[2], IO_DATA_IN[3], IO_DATA_IN[4], IO_DATA_IN[5], IO_DATA_IN[7], IO_DATA_IN[8], IO_DATA_IN[10], IO_DATA_IN[12], IO_DATA_IN[13], IO_DATA_IN[15]}
  // also tied to VCC on the sheet: {IO_DATA_IN[6], IO_DATA_IN[9], IO_DATA_IN[11], IO_DATA_IN[14]}

  // Other names for the same wires on the sheet: ENABLE2 = ENABLE; SHOULD_SAVE_DATA2 = SHOULD_SAVE_DATA
endmodule

module sum1 (
  input  A,
  input  B,
  input  Cin,
  output S,
  output Cout
);

  wire and_1_out, and_2_out, xor_1_out;

  xor xor_1 (xor_1_out, A, B);
  xor xor_2 (S, xor_1_out, Cin);
  and and_1 (and_1_out, xor_1_out, Cin);
  and and_2 (and_2_out, A, B);
  or or_1 (Cout, and_1_out, and_2_out);
endmodule

module sum2 (
  input  [1:0] A,
  input  [1:0] B,
  input  Cin,
  output [1:0] S,
  output Cout
);

  wire sum1_1_cout;

  sum1 sum1_1 (.A(A[0]), .B(B[0]), .Cin(Cin), .S(S[0]), .Cout(sum1_1_cout));
  sum1 sum1_2 (.A(A[1]), .B(B[1]), .Cin(sum1_1_cout), .S(S[1]), .Cout(Cout));
endmodule

module sum4 (
  input  [3:0] A,
  input  [3:0] B,
  input  Cin,
  output [3:0] S,
  output Cout
);

  wire sum2_1_cout;

  sum2 sum2_1 (.A(A[1:0]), .B(B[1:0]), .Cin(Cin), .S(S[1:0]), .Cout(sum2_1_cout));
  sum2 sum2_2 (.A(A[3:2]), .B(B[3:2]), .Cin(sum2_1_cout), .S(S[3:2]), .Cout(Cout));

  // Other names for the same wires on the sheet: A1[1:0] = A[3:2]; B1[1:0] = B[3:2]
endmodule

module sum8 (
  input  [7:0] A,
  input  [7:0] B,
  input  Cin,
  output [7:0] S,
  output Cout
);

  wire sum4_1_cout;

  sum4 sum4_1 (.A(A[3:0]), .B(B[3:0]), .Cin(Cin), .S(S[3:0]), .Cout(sum4_1_cout));
  sum4 sum4_2 (.A(A[7:4]), .B(B[7:4]), .Cin(sum4_1_cout), .S(S[7:4]), .Cout(Cout));

  // Other names for the same wires on the sheet: A1[3:0] = A[7:4]; B1[3:0] = B[7:4]
endmodule

module sum16 (
  input  [15:0] A,
  input  [15:0] B,
  input  Cin,
  output [15:0] S,
  output Cout
);

  wire sum8_1_cout;

  sum8 sum8_1 (.A(A[7:0]), .B(B[7:0]), .Cin(Cin), .S(S[7:0]), .Cout(sum8_1_cout));
  sum8 sum8_2 (.A(A[15:8]), .B(B[15:8]), .Cin(sum8_1_cout), .S(S[15:8]), .Cout(Cout));

  // Other names for the same wires on the sheet: A1[7:0] = A[15:8]; B1[7:0] = B[15:8]
endmodule

module sum32 (
  input  [31:0] A,
  input  [31:0] B,
  input  Cin,
  output [31:0] S,
  output Cout
);

  wire sum16_1_cout;

  sum16 sum16_1 (.A(A[15:0]), .B(B[15:0]), .Cin(Cin), .S(S[15:0]), .Cout(sum16_1_cout));
  sum16 sum16_2 (.A(A[31:16]), .B(B[31:16]), .Cin(sum16_1_cout), .S(S[31:16]), .Cout(Cout));

  // Other names for the same wires on the sheet: A1[15:0] = A[31:16]; B1[15:0] = B[31:16]
endmodule

module input_parser (
  input  [15:0] N,
  output [9:0] Mant,
  output [4:0] Exp,
  output Sign,
  output IS_ZERO,
  output IS_NAN,
  output IS_INF
);

  wire IS_EXP_0, IS_EXP_MAX, M_0, M_NOT_0;

  nor nor_1 (M_0, N[0], N[1], N[2], N[3], N[4], N[5], N[6], N[7], N[8], N[9]);
  not not_1 (M_NOT_0, M_0);
  nor nor_2 (IS_EXP_0, N[10], N[11], N[12], N[13], N[14]);
  and and_1 (IS_EXP_MAX, N[10], N[11], N[12], N[13], N[14]);
  // Probe on IS_EXP_0
  // Probe on IS_EXP_MAX
  and and_2 (IS_ZERO, IS_EXP_0, M_0);
  and and_3 (IS_NAN, M_NOT_0, IS_EXP_MAX);
  and and_4 (IS_INF, M_0, IS_EXP_MAX);

  assign Exp = N[14:10];
  assign Mant = N[9:0];
  assign Sign = N[15];
endmodule

module special_case_handler (
  input  [15:0] N,
  input  Sign,
  input  IS_ZERO_INP,
  input  IS_NAN_INP,
  input  IS_INF_INP,
  output [15:0] SPECIAL_OUT,
  output IS_PINF,
  output IS_NAN,
  output IS_NINF,
  output BYPASS_CORE
);

  wire and_1_out, and_2_out, nand_1_out, not_1_out, not_2_out, not_3_out, or_2_out;
  wire [15:0] mux_2to1_16bit_1_res, mux_2to1_16bit_2_res, or_1_out;

  assign or_1_out = N | 16'h7e00;  // OR_Gate or_1, 16 bits wide
  not not_1 (not_1_out, IS_ZERO_INP);
  nand nand_1 (nand_1_out, not_1_out, Sign);
  or or_2 (or_2_out, IS_ZERO_INP, IS_INF_INP);
  mux_2to1_16bit mux_2to1_16bit_1 (.D1(or_1_out), .COND(IS_NAN_INP), .RES(mux_2to1_16bit_1_res));  // open: D0
  not not_2 (not_2_out, IS_ZERO_INP);
  mux_2to1_16bit mux_2to1_16bit_2 (
    .D1(mux_2to1_16bit_1_res), .D0(16'hfe00), .COND(nand_1_out), .RES(mux_2to1_16bit_2_res));
  not not_3 (not_3_out, Sign);
  and and_1 (and_1_out, Sign, not_2_out);
  and and_2 (and_2_out, Sign, IS_INF_INP);
  and and_3 (IS_PINF, not_3_out, IS_INF_INP);
  or or_3 (IS_NAN, and_1_out, and_2_out, IS_NAN_INP);
  mux_2to1_16bit mux_2to1_16bit_3 (.D1(N), .D0(mux_2to1_16bit_2_res), .COND(or_2_out), .RES(SPECIAL_OUT));
  or or_4 (BYPASS_CORE, IS_PINF, IS_NAN, IS_ZERO_INP);

  assign IS_NINF = 1'b0;
endmodule

module mux_2to1_1bit (
  input  D1,
  input  D0,
  input  COND,
  output RES
);

  wire and_1_out, and_2_out, not_1_out;

  not not_1 (not_1_out, COND);
  and and_1 (and_1_out, D1, COND);
  and and_2 (and_2_out, D0, not_1_out);
  or or_1 (RES, and_1_out, and_2_out);
endmodule

module mux_4to1_1bit (
  input  D3,
  input  D2,
  input  D1,
  input  D0,
  input  S0,
  input  S1,
  output RES
);

  wire mux_2to1_1bit_1_res, mux_2to1_1bit_2_res;

  mux_2to1_1bit mux_2to1_1bit_1 (.D1(D3), .D0(D2), .COND(S0), .RES(mux_2to1_1bit_1_res));
  mux_2to1_1bit mux_2to1_1bit_2 (.D1(D1), .D0(D0), .COND(S0), .RES(mux_2to1_1bit_2_res));
  mux_2to1_1bit mux_2to1_1bit_3 (.D1(mux_2to1_1bit_1_res), .D0(mux_2to1_1bit_2_res), .COND(S1), .RES(RES));
endmodule

module mux_8to1_1bit (
  input  D7,
  input  D6,
  input  D5,
  input  D4,
  input  D3,
  input  D2,
  input  D1,
  input  D0,
  input  S0,
  input  S1,
  input  S2,
  output RES
);

  wire mux_4to1_1bit_1_res, mux_4to1_1bit_2_res;

  mux_4to1_1bit mux_4to1_1bit_1 (.D3(D7), .D2(D6), .D1(D5), .D0(D4), .S0(S0), .S1(S1), .RES(mux_4to1_1bit_1_res));
  mux_4to1_1bit mux_4to1_1bit_2 (.D3(D3), .D2(D2), .D1(D1), .D0(D0), .S0(S0), .S1(S1), .RES(mux_4to1_1bit_2_res));
  mux_2to1_1bit mux_2to1_1bit_1 (.D1(mux_4to1_1bit_1_res), .D0(mux_4to1_1bit_2_res), .COND(S2), .RES(RES));
endmodule

module mux_2to1_16bit (
  input  [15:0] D1,
  input  [15:0] D0,
  input  COND,
  output [15:0] RES
);

  wire [15:0] and_1_out, and_2_out;
  wire [15:15] not_1_out;

  not not_1 (not_1_out[15], COND);
  assign and_1_out = D1 & {16{COND}};  // AND_Gate and_1, 16 bits wide
  assign and_2_out = D0 & {16{not_1_out[15]}};  // AND_Gate and_2, 16 bits wide
  assign RES = and_1_out | and_2_out;  // OR_Gate or_1, 16 bits wide
endmodule

module rs_trigger_sync (
  input  R,
  input  C,
  input  S,
  input  ENABLE,
  output Q,
  output NOT_Q
);

  wire and_1_out, and_2_out, and_3_out, not_1_out, not_2_out, or_1_out, or_2_out;

  not not_1 (not_1_out, ENABLE);
  not not_2 (not_2_out, ENABLE);
  or or_1 (or_1_out, R, not_1_out);
  or or_2 (or_2_out, C, not_2_out);
  and and_1 (and_1_out, S, ENABLE);
  and and_2 (and_2_out, or_1_out, or_2_out);
  and and_3 (and_3_out, or_2_out, and_1_out);
  nor nor_1 (Q, and_2_out, NOT_Q);
  nor nor_2 (NOT_Q, Q, and_3_out);
endmodule

module d_trigger (
  input  D,
  input  C,
  input  ENABLE,
  output Q,
  output NOT_Q
);

  wire not_1_out;

  not not_1 (not_1_out, D);
  rs_trigger_sync rs_trigger_sync_1 (.R(not_1_out), .C(C), .S(D), .ENABLE(ENABLE), .Q(Q), .NOT_Q(NOT_Q));
endmodule

module d_trigger_front (
  input  D,
  input  C,
  input  ENABLE,
  output Q,
  output NOT_Q
);

  wire d_trigger_1_q, not_1_out;

  not not_1 (not_1_out, C);
  d_trigger d_trigger_1 (.D(D), .C(not_1_out), .ENABLE(ENABLE), .Q(d_trigger_1_q));  // open: NOT_Q
  d_trigger d_trigger_2 (.D(d_trigger_1_q), .C(C), .ENABLE(ENABLE), .Q(Q), .NOT_Q(NOT_Q));
endmodule

module memory_2bits (
  input  [1:0] DATA,
  input  C,
  input  ENABLE,
  output [1:0] VAL
);

  d_trigger_front d_trigger_front_1 (.D(DATA[0]), .C(C), .ENABLE(ENABLE), .Q(VAL[0]));  // open: NOT_Q
  d_trigger_front d_trigger_front_2 (.D(DATA[1]), .C(C), .ENABLE(ENABLE), .Q(VAL[1]));  // open: NOT_Q
endmodule

module memory_4bits (
  input  [3:0] DATA,
  input  C,
  input  ENABLE,
  output [3:0] VAL
);

  memory_2bits memory_2bits_1 (.DATA(DATA[1:0]), .C(C), .ENABLE(ENABLE), .VAL(VAL[1:0]));
  memory_2bits memory_2bits_2 (.DATA(DATA[3:2]), .C(C), .ENABLE(ENABLE), .VAL(VAL[3:2]));
endmodule

module memory_8bits (
  input  [7:0] DATA,
  input  C,
  input  ENABLE,
  output [7:0] VAL
);

  memory_4bits memory_4bits_1 (.DATA(DATA[3:0]), .C(C), .ENABLE(ENABLE), .VAL(VAL[3:0]));
  memory_4bits memory_4bits_2 (.DATA(DATA[7:4]), .C(C), .ENABLE(ENABLE), .VAL(VAL[7:4]));
endmodule

module memory_16bits (
  input  [15:0] DATA,
  input  C,
  input  ENABLE,
  output [15:0] VAL
);

  memory_8bits memory_8bits_1 (.DATA(DATA[7:0]), .C(C), .ENABLE(ENABLE), .VAL(VAL[7:0]));
  memory_8bits memory_8bits_2 (.DATA(DATA[15:8]), .C(C), .ENABLE(ENABLE), .VAL(VAL[15:8]));
endmodule

module memory_32bits (
  input  [31:0] DATA,
  input  C,
  input  ENABLE,
  output [31:0] VAL
);

  memory_16bits memory_16bits_1 (.DATA(DATA[15:0]), .C(C), .ENABLE(ENABLE), .VAL(VAL[15:0]));
  memory_16bits memory_16bits_2 (.DATA(DATA[31:16]), .C(C), .ENABLE(ENABLE), .VAL(VAL[31:16]));
endmodule

module clk_counter (
  input  CLK,
  input  ENABLE,
  output [7:0] VAL
);

  wire and_1_out, not_1_out;
  wire [7:0] memory_8bits_1_val, sum8_1_s;

  not not_1 (not_1_out, CLK);
  and and_1 (and_1_out, not_1_out, ENABLE);
  // Probe on memory_8bits_1_val
  memory_8bits memory_8bits_1 (.DATA(sum8_1_s), .C(and_1_out), .ENABLE(ENABLE), .VAL(memory_8bits_1_val));
  sum8 sum8_1 (.A(memory_8bits_1_val), .B(8'h1), .S(sum8_1_s));  // open: Cin, Cout
  sum8 sum8_2 (.A(memory_8bits_1_val), .B({8{1'b1}}), .S(VAL));  // open: Cin, Cout
  // Probe on sum8_1_s
endmodule

module mem_2bits_level (
  input  [1:0] DATA,
  input  C,
  input  ENABLE,
  output [1:0] VAL
);

  d_trigger d_trigger_1 (.D(DATA[0]), .C(C), .ENABLE(ENABLE), .Q(VAL[0]));  // open: NOT_Q
  d_trigger d_trigger_2 (.D(DATA[1]), .C(C), .ENABLE(ENABLE), .Q(VAL[1]));  // open: NOT_Q
endmodule

module mem_4bits_level (
  input  [3:0] DATA,
  input  C,
  input  ENABLE,
  output [3:0] VAL
);

  mem_2bits_level mem_2bits_level_1 (.DATA(DATA[1:0]), .C(C), .ENABLE(ENABLE), .VAL(VAL[1:0]));
  mem_2bits_level mem_2bits_level_2 (.DATA(DATA[3:2]), .C(C), .ENABLE(ENABLE), .VAL(VAL[3:2]));
endmodule

module mem_8bits_level (
  input  [7:0] DATA,
  input  C,
  input  ENABLE,
  output [7:0] VAL
);

  mem_4bits_level mem_4bits_level_1 (.DATA(DATA[3:0]), .C(C), .ENABLE(ENABLE), .VAL(VAL[3:0]));
  mem_4bits_level mem_4bits_level_2 (.DATA(DATA[7:4]), .C(C), .ENABLE(ENABLE), .VAL(VAL[7:4]));
endmodule

module mem_16bits_level (
  input  [15:0] DATA,
  input  C,
  input  ENABLE,
  output [15:0] VAL
);

  mem_8bits_level mem_8bits_level_1 (.DATA(DATA[7:0]), .C(C), .ENABLE(ENABLE), .VAL(VAL[7:0]));
  mem_8bits_level mem_8bits_level_2 (.DATA(DATA[15:8]), .C(C), .ENABLE(ENABLE), .VAL(VAL[15:8]));
endmodule

module mem_32bits_level (
  input  [31:0] DATA,
  input  C,
  input  ENABLE,
  output [31:0] VAL
);

  mem_16bits_level mem_16bits_level_1 (.DATA(DATA[15:0]), .C(C), .ENABLE(ENABLE), .VAL(VAL[15:0]));
  mem_16bits_level mem_16bits_level_2 (.DATA(DATA[31:16]), .C(C), .ENABLE(ENABLE), .VAL(VAL[31:16]));
endmodule

module denorm_mant_shifter (
  input  [9:0] MANT,
  input  ENABLE,
  output [15:0] MANT_SHIFTED
);

  wire not_1_out, or_1_out;
  wire [5:0] undriven;
  wire [15:0] mux_2to1_16bit_1_res;

  or or_1 (or_1_out, 1'b0, MANT_SHIFTED[0], MANT_SHIFTED[1], MANT_SHIFTED[2], MANT_SHIFTED[3], MANT_SHIFTED[4], MANT_SHIFTED[5], MANT_SHIFTED[6], MANT_SHIFTED[7], MANT_SHIFTED[8], MANT_SHIFTED[9], MANT_SHIFTED[10], MANT_SHIFTED[11], MANT_SHIFTED[12], MANT_SHIFTED[13], MANT_SHIFTED[14]);
  mux_2to1_16bit mux_2to1_16bit_1 (
    .D1({MANT_SHIFTED[14:0], 1'b0}), .D0({undriven, MANT}), .COND(or_1_out), .RES(mux_2to1_16bit_1_res));
  // Probe on mux_2to1_16bit_1_res
  not not_1 (not_1_out, MANT_SHIFTED[10]);
  mem_16bits_level mem_16bits_level_1 (.DATA(mux_2to1_16bit_1_res), .C(not_1_out), .ENABLE(ENABLE), .VAL(MANT_SHIFTED));
  // Probe on MANT_SHIFTED

  // Other names for the same wires on the sheet: CYCLE[15:1] = MANT_SHIFTED[14:0]
endmodule

module exp_mant_normalizer (
  input  [9:0] MANT,
  input  [4:0] EXP,
  input  ENABLE,
  output [15:0] NORM_MANT,
  output [4:0] NORM_EXP
);

  wire not_1_out, or_1_out;
  wire [7:5] sum8_1_s, undriven;
  wire [15:0] denorm_mant_shifter_1_mant_shifted;

  // Probe on or_1_out
  or or_1 (or_1_out, EXP[0], EXP[1], EXP[2], EXP[3], EXP[4]);
  // Probe on {undriven, EXP}
  denorm_mant_shifter denorm_mant_shifter_1 (
    .MANT(MANT), .ENABLE(ENABLE), .MANT_SHIFTED(denorm_mant_shifter_1_mant_shifted));
  not not_1 (not_1_out, or_1_out);
  sum8 sum8_1 (.B({undriven, EXP}), .Cin(not_1_out), .S({sum8_1_s, NORM_EXP}));  // open: A, Cout
  mux_2to1_16bit mux_2to1_16bit_1 (
    .D1({6'b000001, MANT}), .D0(denorm_mant_shifter_1_mant_shifted), .COND(or_1_out), .RES(NORM_MANT));
endmodule

module exp_to_odd (
  input  [15:0] MANT,
  input  [4:0] EXP,
  output [15:0] NEW_MANT,
  output [4:0] NEW_EXP
);

  wire [7:0] sum8_1_s;
  wire [7:5] undriven;
  wire [15:5] mux_2to1_16bit_2_res, undriven_2;
  wire [15:8] undriven_3;

  // Probe on EXP[0]
  // Probe on {undriven_2, EXP}
  // Probe on sum8_1_s
  sum8 sum8_1 (.A({undriven, EXP}), .B({8{1'b1}}), .S(sum8_1_s));  // open: Cin, Cout
  // Probe on {undriven_3, sum8_1_s}
  // Probe on NEW_MANT
  mux_2to1_16bit mux_2to1_16bit_1 (.D1(MANT), .D0({MANT[14:0], 1'b0}), .COND(EXP[0]), .RES(NEW_MANT));
  // Probe on {mux_2to1_16bit_2_res, NEW_EXP}
  mux_2to1_16bit mux_2to1_16bit_2 (
    .D1({undriven_2, EXP}), .D0({undriven_3, sum8_1_s}), .COND(EXP[0]), .RES({mux_2to1_16bit_2_res, NEW_EXP}));
endmodule

module mux_2to1_32bit (
  input  [31:0] D1,
  input  [31:0] D0,
  input  COND,
  output [31:0] RES
);

  wire [31:0] and_1_out, and_2_out;
  wire [31:31] not_1_out;

  not not_1 (not_1_out[31], COND);
  assign and_1_out = D1 & {32{COND}};  // AND_Gate and_1, 32 bits wide
  assign and_2_out = D0 & {32{not_1_out[31]}};  // AND_Gate and_2, 32 bits wide
  assign RES = and_1_out | and_2_out;  // OR_Gate or_1, 32 bits wide
endmodule

module right_shift_32bits (
  input  [31:0] VAL,
  input  [4:0] SHIFT,
  output [31:0] RES
);

  wire [31:0] mux_2to1_32bit_1_res, mux_2to1_32bit_2_res, mux_2to1_32bit_3_res, mux_2to1_32bit_4_res;
  wire [31:16] undriven_5;
  wire [31:24] undriven_4;
  wire [31:28] undriven_3;
  wire [31:30] undriven_2;
  wire [31:31] undriven;

  // Probe on mux_2to1_32bit_1_res
  mux_2to1_32bit mux_2to1_32bit_1 (
    .D1({undriven[31], VAL[31:1]}), .D0(VAL), .COND(SHIFT[0]), .RES(mux_2to1_32bit_1_res));
  // Probe on mux_2to1_32bit_2_res
  mux_2to1_32bit mux_2to1_32bit_2 (
    .D1({undriven_2, mux_2to1_32bit_1_res[31:2]}), .D0(mux_2to1_32bit_1_res), .COND(SHIFT[1]),
    .RES(mux_2to1_32bit_2_res));
  // Probe on mux_2to1_32bit_3_res
  mux_2to1_32bit mux_2to1_32bit_3 (
    .D1({undriven_3, mux_2to1_32bit_2_res[31:4]}), .D0(mux_2to1_32bit_2_res), .COND(SHIFT[2]),
    .RES(mux_2to1_32bit_3_res));
  // Probe on mux_2to1_32bit_4_res
  mux_2to1_32bit mux_2to1_32bit_4 (
    .D1({undriven_4, mux_2to1_32bit_3_res[31:8]}), .D0(mux_2to1_32bit_3_res), .COND(SHIFT[3]),
    .RES(mux_2to1_32bit_4_res));
  // Probe on RES
  mux_2to1_32bit mux_2to1_32bit_5 (
    .D1({undriven_5, mux_2to1_32bit_4_res[31:16]}), .D0(mux_2to1_32bit_4_res), .COND(SHIFT[4]), .RES(RES));
endmodule

module left_shift_32bits (
  input  [31:0] VAL,
  input  [4:0] SHIFT,
  output [31:0] RES
);

  wire [0:0] undriven;
  wire [1:0] undriven_2;
  wire [3:0] undriven_3;
  wire [7:0] undriven_4;
  wire [15:0] undriven_5;
  wire [31:0] mux_2to1_32bit_1_res, mux_2to1_32bit_2_res, mux_2to1_32bit_3_res, mux_2to1_32bit_4_res;

  // Probe on mux_2to1_32bit_1_res
  mux_2to1_32bit mux_2to1_32bit_1 (
    .D1({VAL[30:0], undriven[0]}), .D0(VAL), .COND(SHIFT[0]), .RES(mux_2to1_32bit_1_res));
  // Probe on mux_2to1_32bit_2_res
  mux_2to1_32bit mux_2to1_32bit_2 (
    .D1({mux_2to1_32bit_1_res[29:0], undriven_2}), .D0(mux_2to1_32bit_1_res), .COND(SHIFT[1]),
    .RES(mux_2to1_32bit_2_res));
  // Probe on mux_2to1_32bit_3_res
  mux_2to1_32bit mux_2to1_32bit_3 (
    .D1({mux_2to1_32bit_2_res[27:0], undriven_3}), .D0(mux_2to1_32bit_2_res), .COND(SHIFT[2]),
    .RES(mux_2to1_32bit_3_res));
  // Probe on mux_2to1_32bit_4_res
  mux_2to1_32bit mux_2to1_32bit_4 (
    .D1({mux_2to1_32bit_3_res[23:0], undriven_4}), .D0(mux_2to1_32bit_3_res), .COND(SHIFT[3]),
    .RES(mux_2to1_32bit_4_res));
  // Probe on RES
  mux_2to1_32bit mux_2to1_32bit_5 (
    .D1({mux_2to1_32bit_4_res[15:0], undriven_5}), .D0(mux_2to1_32bit_4_res), .COND(SHIFT[4]), .RES(RES));
endmodule

module calc_sqrt (
  input  [15:0] MANT,
  input  [7:0] COUNTER,
  input  CLK,
  input  ENABLE,
  output RESULT,
  output [10:0] MANT_SQRT
);

  wire CLK2, not_1_out, not_2_out, not_3_out, not_6_out, or_1_out;
  wire [0:0] UPDATED_ANSWER;
  wire [7:0] not_4_out, S_22_MINUS_CNTR_MUL_2_s;
  wire [15:0] undriven;
  wire [15:11] ANSWER;
  wire [31:0] left_shift_32bits_1_res, left_shift_32bits_2_res, mux_2to1_32bit_1_res, not_5_out, sum32_1_s,
       UPDATED_VALUE, VALUE;

  not not_1 (not_1_out, COUNTER[0]);
  or or_1 (or_1_out, not_1_out, COUNTER[1], COUNTER[2], COUNTER[3], COUNTER[5], COUNTER[6], COUNTER[7], COUNTER[4]);
  // Probe on left_shift_32bits_1_res
  left_shift_32bits left_shift_32bits_1 (.VAL({undriven, MANT}), .SHIFT(5'b01010), .RES(left_shift_32bits_1_res));
  // Probe on not_2_out
  not not_2 (not_2_out, or_1_out);
  not not_3 (not_3_out, MANT_SQRT[10]);
  // Probe on {ANSWER[14:11], MANT_SQRT, UPDATED_ANSWER[0]}
  and and_1 (CLK2, CLK, not_3_out);
  // Probe on MANT_SQRT[10]
  // Probe on {ANSWER, MANT_SQRT}
  memory_16bits STORING_ANSWER (
    .DATA({ANSWER[14:11], MANT_SQRT, UPDATED_ANSWER[0]}), .C(CLK2), .ENABLE(ENABLE), .VAL({ANSWER, MANT_SQRT}));
  // Probe on {COUNTER[6:0], 1'b0}
  // Probe on mux_2to1_32bit_1_res
  mux_2to1_32bit mux_2to1_32bit_1 (
    .D1(left_shift_32bits_1_res), .D0(UPDATED_VALUE), .COND(not_2_out), .RES(mux_2to1_32bit_1_res));
  assign not_4_out = ~{COUNTER[6:0], 1'b0};  // NOT_Gate not_4, 8 bits wide
  // Probe on S_22_MINUS_CNTR_MUL_2_s
  sum8 S_22_MINUS_CNTR_MUL_2 (.A(8'h18), .B(not_4_out), .Cin(1'b1), .S(S_22_MINUS_CNTR_MUL_2_s));  // open: Cout
  // Probe on VALUE
  memory_32bits STORING_MANT (.DATA(mux_2to1_32bit_1_res), .C(CLK2), .ENABLE(ENABLE), .VAL(VALUE));
  // Probe on {ANSWER[13:11], MANT_SQRT, 2'b01}
  left_shift_32bits left_shift_32bits_2 (
    .VAL({{16{1'b0}}, ANSWER[13:11], MANT_SQRT, 2'b01}), .SHIFT(S_22_MINUS_CNTR_MUL_2_s[4:0]),
    .RES(left_shift_32bits_2_res));
  // Probe on left_shift_32bits_2_res
  // Probe on VALUE
  assign not_5_out = ~left_shift_32bits_2_res;  // NOT_Gate not_5, 32 bits wide
  sum32 sum32_1 (.A(VALUE), .B(not_5_out), .Cin(1'b1), .S(sum32_1_s), .Cout(UPDATED_ANSWER[0]));
  // Probe on UPDATED_ANSWER[0]
  not not_6 (not_6_out, UPDATED_ANSWER[0]);
  // Probe on UPDATED_VALUE
  mux_2to1_32bit mux_2to1_32bit_2 (.D1(VALUE), .D0(sum32_1_s), .COND(not_6_out), .RES(UPDATED_VALUE));

  assign RESULT = MANT_SQRT[10];

  // Other names for the same wires on the sheet: CLK_t = CLK2; ENABLE2 = ENABLE; ANSWER[10:0] = MANT_SQRT;
  //   UPDATED_ANSWER[15:1] = {ANSWER[14:11], MANT_SQRT}
endmodule

module assemble_answer (
  input  [10:0] MANT_SQRT,
  input  [4:0] ODD_EXP,
  output [15:0] ANSWER
);

  not not_1 (ANSWER[13], ODD_EXP[4]);
  // Probe on {ODD_EXP[4], ANSWER[13], ODD_EXP[3:1]}

  assign {ANSWER[15:14], ANSWER[12:0]} = {1'b0, ODD_EXP[4:1], MANT_SQRT[9:0]};
endmodule

module is_strictly_more_32bits (
  input  [31:0] A,
  input  [31:0] B,
  output GT
);

  wire nor_1_out, not_2_out, sum32_1_cout;
  wire [31:0] not_1_out, sum32_1_s;

  assign not_1_out = ~B;  // NOT_Gate not_1, 32 bits wide
  // Probe on sum32_1_s
  sum32 sum32_1 (.A(A), .B(not_1_out), .Cin(1'b1), .S(sum32_1_s), .Cout(sum32_1_cout));
  // Probe on nor_1_out
  nor nor_1 (nor_1_out, sum32_1_s[0], sum32_1_s[1], sum32_1_s[2], sum32_1_s[3], sum32_1_s[4], sum32_1_s[5], sum32_1_s[6], sum32_1_s[7], sum32_1_s[8], sum32_1_s[9], sum32_1_s[10], sum32_1_s[11], sum32_1_s[12], sum32_1_s[13], sum32_1_s[14], sum32_1_s[15], sum32_1_s[17], sum32_1_s[18], sum32_1_s[19], sum32_1_s[20], sum32_1_s[21], sum32_1_s[22], sum32_1_s[23], sum32_1_s[24], sum32_1_s[25], sum32_1_s[26], sum32_1_s[27], sum32_1_s[28], sum32_1_s[29], sum32_1_s[30], sum32_1_s[31], sum32_1_s[16]);
  not not_2 (not_2_out, nor_1_out);
  and and_1 (GT, not_2_out, sum32_1_cout);
endmodule
